// Digital circuit ALU.dig as structural Verilog
module ALU (
  input  [7:0] A,
  input  [7:0] B,
  input  [2:0] Select,
  input  Clock,
  output [7:0] AC,
  output [7:0] MQ
);

  wire [7:0] div_1_r, left_shift_8bit_1_p2, MQ0, MQ1, multiplexer_2_out, multiplicador_8bit_1_p3,
       nand_8bit_1_p3, right_shift_1_p2, S, soma_8bit_1_p4, subtracao_8bit_1_p4, xor_8bit_1_p3;

  // Soma_8bit soma_8bit_1: pin names not known; wires that end beside it: A, B, 1'b0, soma_8bit_1_p4
  // Subtracao_8bit subtracao_8bit_1: pin names not known; wires that end beside it: A, B, 1'b0, subtracao_8bit_1_p4
  // Multiplicador_8bit multiplicador_8bit_1: pin names not known; wires that end beside it: A, B, {MQ0, multiplicador_8bit_1_p3}
  // NAND_8bit nand_8bit_1: pin names not known; wires that end beside it: A, B, nand_8bit_1_p3
  // XOR_8bit xor_8bit_1: pin names not known; wires that end beside it: A, B, xor_8bit_1_p3
  // Left_Shift_8bit left_shift_8bit_1: pin names not known; wires that end beside it: A, left_shift_8bit_1_p2
  // Right_Shift right_shift_1: pin names not known; wires that end beside it: A, right_shift_1_p2
  Div #(.Bits(8)) div_1 (.a(A), .b(B), .q(MQ1), .r(div_1_r));
  Multiplexer #(.Selector_Bits(3), .Bits(8)) multiplexer_1 (
    .sel(Select), .in_0(soma_8bit_1_p4), .in_1(subtracao_8bit_1_p4), .in_2(multiplicador_8bit_1_p3),
    .in_3(nand_8bit_1_p3), .in_4(xor_8bit_1_p3), .in_5(left_shift_8bit_1_p2), .in_6(right_shift_1_p2),
    .in_7(div_1_r), .out(S));
  Multiplexer #(.Selector_Bits(3), .Bits(8)) multiplexer_2 (
    .sel(Select), .in_0(MQ), .in_1(MQ), .in_2(MQ0), .in_3(MQ), .in_4(MQ), .in_5(MQ), .in_6(MQ), .in_7(MQ1),
    .out(multiplexer_2_out));
  Register #(.Bits(8)) u_AC (.D(S), .C(Clock), .en(1'b1), .Q(AC));
  Register #(.Bits(8)) u_MQ (.D(multiplexer_2_out), .C(Clock), .en(1'b1), .Q(MQ));

  // Other names for the same wires on the sheet: CLK = Clock
endmodule
