// Digital circuit CPU_com_barramento.dig as structural Verilog
module CPU_com_barramento (
  input  Clock,
  output [7:0] AC,
  output [7:0] MQ
);

  wire comparator_1_eq, not_1_out, not_2_out, reset, Storage;
  wire [2:0] OpCode;
  wire [7:0] driver_1_out, driver_3_out, eepromdualport_1_d, PC_out;

  Comparator #(.Bits(8)) u_reset (.a(8'h5), .b(PC_out), .eq(reset));  // open: gt, lt
  Counter #(.Bits(8)) counter_1 (.en(1'b1), .C(Clock), .clr(reset), .out(PC_out));  // open: ovf
  EEPROMDualPort #(.AddrBits(8), .Bits(8)) eepromdualport_1 (
    .A(PC_out), .Din(driver_1_out), .str(Storage), .C(Clock), .ld(1'b1), .D(eepromdualport_1_d));
  ROM #(.AddrBits(3), .Bits(3)) u_OpCode (.A(PC_out[2:0]), .sel(1'b1), .D(OpCode));
  not not_1 (not_1_out, Storage);
  assign driver_1_out = not_1_out ? eepromdualport_1_d : 8'bz;  // Driver driver_1
  assign driver_1_out = Storage ? AC : 8'bz;  // Driver driver_2
  Comparator #(.Bits(3)) comparator_1 (.a(3'b101), .b(OpCode), .eq(comparator_1_eq));  // open: gt, lt
  not not_2 (not_2_out, Storage);
  assign driver_3_out = not_2_out ? driver_1_out : 8'bz;  // Driver driver_3
  and and_1 (Storage, comparator_1_eq, Clock);
  ALU alu_1 (.A({8{1'b0}}), .B(driver_3_out), .Select(OpCode), .Clock(Clock), .AC(AC), .MQ(MQ));

  // Notes on the sheet:
  //   contents of eepromdualport_1 (hex, n*v repeats v):
  //   2,4,6,8,a
  //   contents of OpCode (hex, n*v repeats v):
  //   7*0,5
endmodule
